# Fritzing sketch Flagging Circuit (saved by Fritzing 0.8.7b)
breadboards: 1

parts:
  LM7805 = Voltage Regulator [package=to-220-alt]
  1mF = Capacitor [package=cap-pth-small-kit]
  Arm = Basic Servo
  Magnet_Feeder = Basic Servo
  Flagging_Arduino = Arduino Uno (Rev3)
  N-Channel_Mosfet = Basic FET N-Channel [package="D2Pak [SMD]"]
  part = Battery block 9V
  12V = Battery block 9V
  12V_Electromagnet = Solenoid

nets:
  GND: LM7805.GND, 1mF.2, Arm.gnd, Magnet_Feeder.gnd, Flagging_Arduino.GND, N-Channel_Mosfet.source, part.+, 12V.-
  N1: LM7805.IN, part.-
  VCC: LM7805.OUT, 1mF.1, Arm.vcc, Magnet_Feeder.vcc
  N2: Arm.pulse, Flagging_Arduino.D9_PWM
  N3: Magnet_Feeder.pulse, Flagging_Arduino.D10_PWM/SS
  N4: Flagging_Arduino.D6_PWM, N-Channel_Mosfet.Gate
  N5: N-Channel_Mosfet.drain, 12V_Electromagnet.pin2
  N6: 12V.+, 12V_Electromagnet.pin1
