# Fritzing sketch red_bull_steering (saved by Fritzing 0.8.7b)
breadboards: 1

parts:
  Part1 = Arduino Uno (Rev3)
  U1 = L298 [package=multiwatt15]
  US1 = SRF05 Ultrasonic Rangefinder
  US3 = SRF05 Ultrasonic Rangefinder
  US2 = SRF05 Ultrasonic Rangefinder
  M_L = DC Motor
  M_R = DC Motor
  S1 = Pushbutton [package="[THT]"]
  LED1 = LED - 5mm [color="Red (633nm)" package="5 mm [THT]"]
  D1 = Diode [package=diode-1n4001]
  D2 = Diode [package=diode-1n4001]
  D3 = Diode [package=diode-1n4001]
  D4 = Diode [package=diode-1n4001]
  D5 = Diode [package=diode-1n4001]
  D6 = Diode [package=diode-1n4001]
  D7 = Diode [package=diode-1n4001]
  D8 = Diode [package=diode-1n4001]
  U2 = MPR121 [package=qfn-20-0.4mm]
  R2 = Resistor [tolerance=±5% resistance=150 package="0805 [SMD]"]
  R3 = Resistor [tolerance=±5% resistance=1k package="0805 [SMD]"]

nets:
  N1: Part1.A0, U1.IN4
  N2: Part1.A1, U1.IN2
  N3: Part1.A2, S1.Pin_3, S1.Pin_4, R3.Pin_0
  N4: Part1.A3, LED1.anode
  N5: Part1.D8, US3.Echo
  N6: Part1.D9_PWM, US3.Trig
  N7: Part1.D10_PWM/SS, US2.Echo
  N8: Part1.D11_PWM/MOSI, US2.Trig
  N9: Part1.D12/MISO, US1.Echo
  N10: Part1.D13/SCK, US1.Trig
  GND: Part1.GND, U1.CSA, U1.GND, U1.CSB, US1.GND, US3.GND, US2.GND, D3.A, D5.A, D6.A, D8.A, U2.REXT, R2.Pin_1, R3.Pin_1
  N11: Part1.A4/SDA, U2.SDA
  N12: Part1.A5/SCL, U2.SCL
  N13: Part1.D2, U2.~IRQ
  N14: Part1.D4, U1.IN3
  N15: Part1.D5_PWM, U1.ENA
  N16: Part1.D6_PWM, U1.ENB
  N17: Part1.D7, U1.IN1
  3V3: Part1.3V3, U2.VSS
  12V: Part1.VIN, U1.VS, D1.C, D2.C, D4.C, D7.C
  N18: U1.OUT1, M_R.pin_1, D1.A, D3.C
  N19: U1.OUT2, M_R.pin_2, D2.A, D5.C
  VCC: U1.VLS, US1.VCC, US3.VCC, US2.VCC, S1.Pin_1
  N20: U1.OUT3, M_L.pin_1, D7.A, D8.C
  N21: U1.OUT4, M_L.pin_2, D4.A, D6.C
  N22: LED1.cathode, R2.Pin_0
